# Fritzing sketch Shade Controller - Base (saved by Fritzing 0.9.4)
perfboards: 2

parts:
  M1 = DOIT Esp32 DevKit v1 (30 pins long, 11 pins width) [part_number=ESP32S-PIN30]
  J1 = female pin header, 2 pins [form="♀ (female)"]
  J2 = female pin header, 2 pins [form="♀ (female)"]
  J3 = female pin header, 2 pins [form="♀ (female)"]
  J4 = female pin header, 2 pins [form="♀ (female)"]
  U1 = Mini-360 DC-DC Buck converter [package=THT]
  S1 = SWITCH-MOMENTARY-2 [package=tactile-pth-12mm]
  S2 = SWITCH-MOMENTARY-2 [package=tactile-pth-12mm]
  J6 = Screw terminal - 2 pins [package=THT]
  J7 = Screw terminal - 2 pins [package=THT]
  J8 = female pin header, 2 pins [form="♀ (female)"]
  J9 = female pin header, 2 pins [form="♀ (female)"]
  U2 = LIPO-1000mAh [package=lipo-1000]
  J5 = Basic Servo

nets:
  N1: M1.GND, U1.OUT-, J8.pin2
  N2: M1.D15, J8.pin1, J9.pin2
  N3: M1.D5, J9.pin1
  N4: M1.D13, J1.pin1, J5.pulse
  N5: M1.VIN, U1.OUT+
  N6: J1.pin2, J2.pin1, J3.pin1, J4.pin2, U1.IN+, U2.+, J5.vcc
  N7: J2.pin2, J3.pin2, U1.IN-, U2.-, J5.gnd
  N8: S1.1, S2.1, J6.pin1
  N9: S1.2, J6.pin2, J7.pin1
  N10: S2.2, J7.pin2

custom parts:
  DOIT Esp32 DevKit v1 (30 pins long, 11 pins width): The DOIT Esp32 DevKit v1 is one of the development board created by DOIT to evaluate the ESP-WROOM-32 module. It is based on the ESP32 microcontroller that boasts Wifi, Bluetooth, Ethernet and Low Power support all in a single chip. (vanepp) made breadboard work, adjusted pin numbering and labels and reduced size of schematic and cleaned up pcb. This chip is 30pins long (2 x15) and 11 pins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
  Mini-360 DC-DC Buck converter: Mini-360 DC-DC Buck converter. Tiny buck step down voltage converter, input voltage 4.75 to 23V output 1 to 17V adjustable. Available from ebay and the like.
