# Fritzing sketch Shade Controller - NFC (saved by Fritzing 0.9.4)
perfboards: 1

parts:
  U3 = Mini-360 DC-DC Buck converter [package=THT]
  Part1 = PN532
  R1 = Resistor [tolerance=±5% resistance=220 package=THT]
  R2 = Resistor [tolerance=±5% resistance=220 package=THT]
  R3 = Resistor [tolerance=±5% resistance=220 package=THT]
  R4 = Resistor [tolerance=±5% resistance=220 package=THT]
  R5 = Resistor [tolerance=±5% resistance=220 package=THT]
  J18 = female pin header, 6 pins [form="♀ (female)"]
  J15 = female pin header, 3 pins [form="♀ (female)"]
  J19 = Screw terminal - 2 pins [package=THT]
  M2 = DOIT Esp32 DevKit v1 (30 pins long, 11 pins width) [part_number=ESP32S-PIN30]
  J11 = female pin header, 3 pins [form="♀ (female)"]
  R6 = Resistor [tolerance=±5% resistance=220 package=THT]
  J20 = female pin header, 3 pins [form="♀ (female)"]
  JACK1 = 2.1mm DC Barrel Jack
  J16 = Basic Servo

nets:
  N1: U3.IN-, J19.pin2
  N2: U3.IN+, J19.pin1
  N3: U3.OUT+, M2.VIN, J20.pin3
  N4: U3.OUT-, M2.GND, J11.pin2, J20.pin2
  N5: Part1.connector1, J18.pin1
  N6: Part1.connector2, J18.pin2
  N7: Part1.connector3, J18.pin3, M2.D21
  N8: Part1.connector4, J18.pin4, M2.D22
  N9: Part1.connector11, J18.pin5, M2.D2
  N10: Part1.connector12, J18.pin6, M2.D4
  N11: R1.Pin_1, R2.Pin_1
  N12: R2.Pin_0, R3.Pin_0
  N13: R3.Pin_1, M2.3V3
  N14: R4.Pin_1, R5.Pin_1
  N15: R5.Pin_0, R6.Pin_0
  N16: J15.pin1, JACK1.center, J16.gnd
  N17: J15.pin2, JACK1.switch, J16.vcc
  N18: J15.pin3, M2.D13, J16.pulse
  N19: M2.D15, J11.pin1

custom parts:
  Mini-360 DC-DC Buck converter: Mini-360 DC-DC Buck converter. Tiny buck step down voltage converter, input voltage 4.75 to 23V output 1 to 17V adjustable. Available from ebay and the like.
  DOIT Esp32 DevKit v1 (30 pins long, 11 pins width): The DOIT Esp32 DevKit v1 is one of the development board created by DOIT to evaluate the ESP-WROOM-32 module. It is based on the ESP32 microcontroller that boasts Wifi, Bluetooth, Ethernet and Low Power support all in a single chip. (vanepp) made breadboard work, adjusted pin numbering and labels and reduced size of schematic and cleaned up pcb. This chip is 30pins long (2 x15) and 11 pins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
  2.1mm DC Barrel Jack: 2.1mm DC Barrel Jack with Thru-Hole Connectors (breadboardable)
